# Fritzing sketch study_timer_circuit (saved by Fritzing 1.0.3b)
circuit board: 8.46667cm x 5.64444cm
breadboards: 3

parts:
  SG1 = Buzzer 12mm [package=buzzer-ccv-kit]
  R1 = Resistor [tolerance=±5% power=0.25W resistance=220 package=THT]
  R2 = Resistor [tolerance=±5% power=0.25W resistance=220 package=THT]
  R3 = Resistor [tolerance=±5% power=0.25W resistance=220 package=THT]
  R4 = Resistor [tolerance=±5% power=0.25W resistance=220 package=THT]
  R5 = Resistor [tolerance=±5% power=0.25W resistance=220 package=THT]
  R6 = Resistor [tolerance=±5% power=0.25W resistance=220 package=THT]
  R7 = Resistor [tolerance=±5% power=0.25W resistance=220 package=THT]
  R8 = Resistor [tolerance=±5% power=0.25W resistance=220 package=THT]
  R9 = Resistor [tolerance=±5% power=0.25W resistance=220 package=THT]
  R10 = Resistor [tolerance=±5% power=0.25W resistance=220 package=THT]
  R11 = Resistor [tolerance=±5% power=0.25W resistance=2000 package=THT]
  Q1 = NPN-Transistor [package="TO92 [THT]"]
  LED1 = RGB LED (com. cathode, rbg) [color="Red (633nm)" current=0.030A package="5 mm [THT]"]
  LED2 = 7-SEGMENT-4DIGIT-YOUNGSUN [package=7-segment-4digit-youngsun]
  U1 = 74HC595 [package="DIP16 [THT]"]
  R12 = Rotary Potentiometer (Large) [maximum_resistance=10kΩ knob_status=50% power=0.5W package=THT]
  S1 = SWITCH-MOMENTARY-2 [package=tactile-pth-12mm]
  J1 = STM32 Nucleo boards

nets:
  VCC: SG1.1, U1.VCC, R12.leg1, J1.5V
  N1: SG1.2, Q1.C
  N2: R1.Pin_0, U1.Q1
  N3: R1.Pin_1, LED2.B
  N4: R2.Pin_0, U1.Q2
  N5: R2.Pin_1, LED2.C
  N6: R3.Pin_0, U1.Q3
  N7: R3.Pin_1, LED2.D
  N8: R4.Pin_0, U1.Q4
  N9: R4.Pin_1, LED2.E
  N10: R5.Pin_0, U1.Q5
  N11: R5.Pin_1, LED2.F
  N12: R6.Pin_0, U1.Q7
  N13: R6.Pin_1, LED2.G
  N14: R7.Pin_0, U1.Q0
  N15: R7.Pin_1, LED2.A
  N16: R8.Pin_0, J1.D4
  N17: R9.Pin_0, J1.D7
  N18: R9.Pin_1, LED1.common_cathode
  N19: R10.Pin_0, J1.D2
  N20: R10.Pin_1, LED1.green_anode
  N21: R11.Pin_0, J1.D3_PWM
  N22: R11.Pin_1, Q1.B
  GND: Q1.E, LED1.blue_anode, LED2.DIG1, U1.GND, R12.leg2, S1.2, J1.GND
  N23: U1.SH_CP, J1.D9_PWM
  N24: U1.ST_CP, J1.D8
  N25: U1.DS, J1.D10_PWM/SS
  N26: R12.wiper, J1.A4/SDA
  N27: S1.1, J1.A0
